# Fritzing sketch arduinoreceive (saved by Fritzing 0.8.7b)
breadboards: 1

parts:
  Componente2 = Arduino Uno (Rev3)
  Componente4 = Logic Level Converter
  BT1 = Bluetooth HC-06u [package=THT]
  J1 = Basic Servo
  J2 = Basic Servo
  NRF24L2 = NRF24L01

nets:
  N1: Componente2.D8, NRF24L2.CSN
  N2: Componente2.D9_PWM, J1.pulse
  N3: Componente2.D11_PWM/MOSI, NRF24L2.MOSI
  N4: Componente2.D12/MISO, NRF24L2.MISO
  N5: Componente2.D13/SCK, NRF24L2.SCK
  GND: Componente2.GND, Componente4.GND, BT1.GND, J1.gnd, NRF24L2.GND
  N6: Componente2.D0/RX, Componente4.RX_HV
  N7: Componente2.D1/TX, Componente4.TX_HV
  N8: Componente2.D3_PWM, J2.pulse
  N9: Componente2.D7, NRF24L2.CE
  3V3: Componente2.3V3, Componente4.LV, NRF24L2.VCC
  N10: Componente4.RX_LV, BT1.RXD
  N11: Componente4.TX_LV, BT1.TXD

custom parts:
  Bluetooth HC-06u: Bluetooth HC-06 - face up, pins down 16.5mm x 37.5mm PCB
  NRF24L01: NRF24L01 module
